# Fritzing sketch NodeMCU_CENTRAL_V01 (saved by Fritzing 0.9.3b)
circuit board: 5.6cm x 3.82cm
breadboards: 1

parts:
  LED1 = LED - 3mm [color="Red (633nm)" package="3 mm [THT]"]
  J1 = Piezo Speaker
  U1 = NodeMCU V1.0
  R1 = Resistor [tolerance=±5% resistance=220 package="2010 [SMD]"]
  R2 = Resistor [tolerance=±5% resistance=10k package="2010 [SMD]"]
  S4 = Pushbutton [package="[SMD]"]
  JP1 = Header 4 [package=molex-1x4_lock]

nets:
  N1: LED1.cathode, R1.Pin_0
  N2: LED1.anode, U1.D3
  N3: J1.pin1, U1.GND, R1.Pin_1, R2.Pin_1, JP1.1
  N4: J1.pin2, U1.D5
  N5: U1.D0, R2.Pin_0, S4.Pin_1, S4.Pin_2
  N6: U1.D1, JP1.3
  N7: U1.D2, JP1.4
  N8: U1.3V3, S4.Pin_3, S4.Pin_4, JP1.2

custom parts:
  NodeMCU V1.0: ESP8266 based NodeMCU
