# Fritzing sketch NodeMCU_EMISOR_V01 (saved by Fritzing 0.9.3b)
breadboards: 1

parts:
  LED1 = LED - 3mm [color="Red (633nm)" package="3 mm [THT]"]
  R1 = Resistor [tolerance=±5% resistance=220 package="2010 [SMD]"]
  S4 = Pushbutton [package="[SMD]"]
  R2 = Resistor [tolerance=±5% resistance=10k package="2010 [SMD]"]
  U2 = NodeMCU V1.0

nets:
  N1: LED1.cathode, R1.Pin_0
  N2: LED1.anode, U2.D1
  N3: R1.Pin_1, R2.Pin_1, U2.GND
  N4: S4.Pin_1, S4.Pin_2, R2.Pin_0, U2.D0
  N5: S4.Pin_3, S4.Pin_4, U2.3V3

custom parts:
  NodeMCU V1.0: ESP8266 based NodeMCU
