# Fritzing sketch NodeMCU_estacion (saved by Fritzing 0.9.3b)
circuit board: 8.46667cm x 5.64444cm
breadboards: 1

parts:
  U1 = ESP8266 NodeMCU LoLin module
  S2 = Pushbutton [package="[THT]"]
  LED1 = smd LED [color="Red (633nm)" package="1206 [SMD]"]
  R1 = Resistor [tolerance=±5% resistance=100 package="0805 [SMD]"]
  R2 = Resistor [tolerance=±5% resistance=10k package="0805 [SMD]"]

nets:
  N1: U1.D1, LED1.anode
  N2: U1.D2, S2.Pin_3, S2.Pin_4, R2.Pin_0
  N3: U1.D5, U1.S0
  N4: U1.3V3, S2.Pin_1, S2.Pin_2
  N5: U1.GND, R1.Pin_1, R2.Pin_1
  N6: LED1.cathode, R1.Pin_0

notes:
  LED 5 // D1 (gpio5)
  BUTTON 4 //D2 (gpio4)

custom parts:
  ESP8266 NodeMCU LoLin module: ESP8266 based NodeMCU
