# Fritzing sketch sem_acustico (saved by Fritzing 0.9.3b)
breadboards: 1

parts:
  Componente1 = Arduino Uno (Rev3)
  U1 = POT [package=pot_mammoth]  # not connected
  LED4 = RGB LED (com. anode, rbg) [package="5 mm [THT]"]
  R1 = Resistor [tolerance=±5% resistance=100 package="0603 [SMD]"]
  Componente2 = Breakout Board for Electret Microphone

nets:
  N1: Componente1.A5/SCL, Componente2.AUD
  GND: Componente1.GND, R1.Pin_0, Componente2.GND
  N2: Componente1.D3_PWM, LED4.red_cathode
  N3: Componente1.D5_PWM, LED4.blue_cathode
  N4: Componente1.D6_PWM, LED4.green_cathode
  5V: Componente1.5V, Componente2.VCC
  N5: LED4.common_anode, R1.Pin_1

notes:
  LED RGB de catodo comun
