# Fritzing sketch Esquema_NodeMCU_05 (saved by Fritzing 0.9.3b)
breadboards: 1

parts:
  U1 = ESP8266 NodeMCU LoLin base
  LED1 = LED - 3mm [color="Red (633nm)" package="3 mm [THT]"]
  R1 = Resistor [tolerance=±5% resistance=220 package="2010 [SMD]"]

nets:
  N1: U1.D1-0, U1.D1-2, LED1.anode
  N2: U1.GND3-0, U1.GND8-8, R1.Pin_1
  N3: LED1.cathode, R1.Pin_0

custom parts:
  ESP8266 NodeMCU LoLin base: ESP8266 based NodeMCU Base
