# Fritzing sketch NodeMCU_previo (saved by Fritzing 0.9.3b)
breadboards: 1

parts:
  U1 = ESP8266 NodeMCU LoLin base
  LED1 = LED - 3mm [color="Red (633nm)" package="3 mm [THT]"]
  R1 = Resistor [tolerance=±5% resistance=220 package="2010 [SMD]"]
  S4 = Pushbutton [package="[SMD]"]
  R2 = Resistor [tolerance=±5% resistance=10k package="2010 [SMD]"]

nets:
  N1: U1.GND1-0, U1.GND8-8, R1.Pin_1, R2.Pin_1
  N2: U1.3V1-0, S4.Pin_3, S4.Pin_4
  N3: U1.D0-0, U1.D0-3, S4.Pin_1, S4.Pin_2, R2.Pin_0
  N4: U1.D1-0, U1.D1-2, LED1.anode
  N5: LED1.cathode, R1.Pin_0

custom parts:
  ESP8266 NodeMCU LoLin base: ESP8266 based NodeMCU Base
